# Fritzing sketch Diagrama (saved by Fritzing 0.9.3b)
breadboards: 1

parts:
  Componente1 = Logic Level Converter  # not connected
  Componente2 = SparkFun ESP8266 Thing
  J1 = Piezo Speaker
  LED1 = LED - 5mm [color="Red (633nm)" package="5 mm [THT]"]
  LED2 = LED - 5mm [color="Blue (470nm)" package="5 mm [THT]"]
  LED3 = LED - 5mm [color="Green (555nm)" package="5 mm [THT]"]
  R1 = Resistor [tolerance=±5% resistance=330 package=THT]
  R2 = Resistor [tolerance=±5% resistance=330 package=THT]
  R3 = Resistor [tolerance=±5% resistance=330 package=THT]
  J2 = screw terminal, 3 pins
  J3 = screw terminal, 3 pins
  J4 = screw terminal, 3 pins
  Q1 = PNP-Transistor [package="TO92 [THT]"]
  R4 = Resistor [tolerance=±5% resistance=220 package=THT]

nets:
  N1: Componente2.GND, R1.Pin_1, R2.Pin_1, R3.Pin_1, J2.pin1, J4.pin1, Q1.E
  N2: Componente2.VCC, J1.pin2
  N3: Componente2.GPIO14, R4.Pin_1
  N4: Componente2.USBVCC, J3.pin2
  N5: Componente2.VIN, J4.pin2
  N6: Componente2.GPIO0, LED1.anode
  N7: Componente2.GPIO4, LED2.anode
  N8: Componente2.GPIO15, LED3.anode
  N9: J1.pin1, Q1.C
  N10: LED1.cathode, R1.Pin_0
  N11: LED2.cathode, R2.Pin_0
  N12: LED3.cathode, R3.Pin_0
  N13: J3.pin3, J4.pin3
  N14: Q1.B, R4.Pin_0

notes:
  GND
  CLK
  SER
  5V
  12V
  LAT
  Poder
  Display
  Buzzer
  Led Indicador
